// Logisim project e2448025.circ as structural Verilog: 1 circuit, main circuit main
module main (
  input  in_1,
  input  in_2,
  input  in_3,
  input  A1,
  input  A0,
  input  B1,
  input  B0,
  input  in_8,
  input  in_9,
  input  in_10,
  output L0,
  output L0_2,
  output L1,
  output S,
  output L2,
  output L3,
  output L4,
  output L5,
  output L6
);

  wire and_1_out, and_2_out, and_3_out, and_4_out, and_5_out, and_6_out, and_7_out, and_8_out, and_9_out,
       and_10_out, and_11_out, and_12_out, and_13_out, and_14_out, and_15_out, and_16_out, and_17_out,
       and_18_out, and_19_out, and_20_out, and_21_out, and_22_out, and_23_out, and_24_out, and_25_out,
       and_26_out, and_27_out, n3_to_8_decoder_74138_1_p7, n3_to_8_decoder_74138_1_p8,
       n3_to_8_decoder_74138_1_p9, n3_to_8_decoder_74138_1_p10, n3_to_8_decoder_74138_1_p11,
       n3_to_8_decoder_74138_1_p12, n3_to_8_decoder_74138_1_p13, n3_to_8_decoder_74138_2_p7,
       n3_to_8_decoder_74138_2_p8, n3_to_8_decoder_74138_2_p9, n3_to_8_decoder_74138_2_p10,
       n3_to_8_decoder_74138_2_p11, n3_to_8_decoder_74138_2_p12, n3_to_8_decoder_74138_2_p13,
       n3_to_8_decoder_74138_3_p7, n3_to_8_decoder_74138_3_p8, n3_to_8_decoder_74138_3_p9,
       n3_to_8_decoder_74138_3_p10, n3_to_8_decoder_74138_3_p11, n3_to_8_decoder_74138_3_p12,
       n3_to_8_decoder_74138_3_p13, n3_to_8_decoder_74138_4_p7, n3_to_8_decoder_74138_4_p8,
       n3_to_8_decoder_74138_4_p9, n3_to_8_decoder_74138_4_p10, n3_to_8_decoder_74138_4_p11,
       n3_to_8_decoder_74138_4_p12, n3_to_8_decoder_74138_4_p13, n3_to_8_decoder_74138_5_p4,
       n3_to_8_decoder_74138_5_p5, n3_to_8_decoder_74138_6_p7, n3_to_8_decoder_74138_6_p8,
       n3_to_8_decoder_74138_6_p9, n3_to_8_decoder_74138_6_p10, n3_to_8_decoder_74138_7_p7,
       n3_to_8_decoder_74138_7_p8, n3_to_8_decoder_74138_7_p9, n3_to_8_decoder_74138_7_p10,
       n3_to_8_decoder_74138_8_p10, n3_to_8_decoder_74138_8_p11, n3_to_8_decoder_74138_8_p12,
       n3_to_8_decoder_74138_8_p13, n4_to_1_mux_x2_74153_1_p13, n4_to_1_mux_x2_74153_1_p14,
       n4_to_1_mux_x2_74153_2_p13, n4_to_1_mux_x2_74153_2_p14, n4_to_1_mux_x2_74153_3_p9,
       n4_to_1_mux_x2_74153_3_p14, n4_to_1_mux_x2_74153_3_p15, n4_to_1_mux_x2_74153_4_p13,
       n4_to_1_mux_x2_74153_4_p14, n4_to_1_mux_x2_74153_5_p13, n4_to_1_mux_x2_74153_5_p14,
       n4_to_1_mux_x2_74153_6_p9, n4_to_1_mux_x2_74153_7_p9, nor_1_out, nor_2_out, nor_3_out, not_1_out,
       not_2_out, not_3_out, not_4_out, not_5_out, not_6_out, not_7_out, not_9_out, not_10_out, not_11_out,
       not_12_out, not_13_out, xor_1_out, xor_2_out;

  // _3_to_8_decoder__74138 #(.Facing("east")) 3_to_8_decoder_74138_1: pin names not known; wires that end beside it: in_3, in_2, in_1, 1'b1, 1'b0, 1'b0, n3_to_8_decoder_74138_1_p7, n3_to_8_decoder_74138_1_p8, n3_to_8_decoder_74138_1_p9, n3_to_8_decoder_74138_1_p10, n3_to_8_decoder_74138_1_p11, n3_to_8_decoder_74138_1_p12, n3_to_8_decoder_74138_1_p13
  nor nor_1 (nor_1_out, A1, A0);
  not not_1 (not_1_out, A0);
  not not_2 (not_2_out, 1'b0);
  not not_3 (not_3_out, 1'b0);
  not not_4 (not_4_out, 1'b0);
  not not_5 (not_5_out, 1'b0);
  not not_6 (not_6_out, A0);
  not not_7 (not_7_out, A1);
  // _4_to_1_MUX__x2___74153 #(.Facing("east")) 4_to_1_mux_x2_74153_1: pin names not known; wires that end beside it: 1'b0, not_2_out, not_2_out, 1'b0, 1'b0, 1'b0, 1'b0, not_2_out, 1'b0, A0, 1'b0, B0, n4_to_1_mux_x2_74153_1_p13, n4_to_1_mux_x2_74153_1_p14
  // _4_to_1_MUX__x2___74153 #(.Facing("east")) 4_to_1_mux_x2_74153_2: pin names not known; wires that end beside it: 1'b0, not_3_out, not_4_out, 1'b0, 1'b0, not_5_out, 1'b0, 1'b0, in_8, A0, in_8, B0, n4_to_1_mux_x2_74153_2_p13, n4_to_1_mux_x2_74153_2_p14
  // _4_to_1_MUX__x2___74153 #(.Facing("east")) 4_to_1_mux_x2_74153_3: pin names not known; wires that end beside it: A1, 1'b0, nor_1_out, 1'b0, not_1_out, 1'b0, A0, not_1_out, n4_to_1_mux_x2_74153_3_p9, in_10, B0, in_10, B1, n4_to_1_mux_x2_74153_3_p14, n4_to_1_mux_x2_74153_3_p15
  not not_8 (n4_to_1_mux_x2_74153_3_p9, 1'b0);
  and and_1 (and_1_out, A0, A1);
  not not_9 (not_9_out, n4_to_1_mux_x2_74153_1_p14);
  not not_10 (not_10_out, 1'b0);
  not not_11 (not_11_out, n4_to_1_mux_x2_74153_2_p14);
  not not_12 (not_12_out, 1'b0);
  and and_2 (and_2_out, not_6_out, not_7_out);
  not not_13 (not_13_out, and_1_out);
  // _4_to_1_MUX__x2___74153 #(.Facing("east")) 4_to_1_mux_x2_74153_4: pin names not known; wires that end beside it: n4_to_1_mux_x2_74153_1_p14, not_9_out, not_9_out, n4_to_1_mux_x2_74153_1_p14, 1'b0, n4_to_1_mux_x2_74153_1_p14, n4_to_1_mux_x2_74153_1_p14, not_10_out, 1'b0, A1, 1'b0, B1, n4_to_1_mux_x2_74153_4_p13, n4_to_1_mux_x2_74153_4_p14
  // _4_to_1_MUX__x2___74153 #(.Facing("east")) 4_to_1_mux_x2_74153_5: pin names not known; wires that end beside it: n4_to_1_mux_x2_74153_2_p14, not_11_out, not_11_out, n4_to_1_mux_x2_74153_2_p14, n4_to_1_mux_x2_74153_2_p14, not_12_out, 1'b0, n4_to_1_mux_x2_74153_2_p14, in_9, A1, in_9, B1, n4_to_1_mux_x2_74153_5_p13, n4_to_1_mux_x2_74153_5_p14
  // _4_to_1_MUX__x2___74153 #(.Facing("east")) 4_to_1_mux_x2_74153_6: pin names not known; wires that end beside it: 1'b0, A1, A0, A0, 1'b1, B0, 1'b0, B1, n4_to_1_mux_x2_74153_6_p9
  xor xor_1 (xor_1_out, B0, A0);
  xor xor_2 (xor_2_out, B1, A1);
  and and_3 (and_3_out, B0, A0);
  and and_4 (and_4_out, B1, A1);
  nor nor_2 (nor_2_out, B0, A0);
  nor nor_3 (nor_3_out, B1, A1);
  // _4_to_1_MUX__x2___74153 #(.Facing("east")) 4_to_1_mux_x2_74153_7: pin names not known; wires that end beside it: and_2_out, not_7_out, not_13_out, 1'b1, n3_to_8_decoder_74138_1_p10, B0, 1'b0, B1, n4_to_1_mux_x2_74153_7_p9
  // _3_to_8_decoder__74138 #(.Facing("east")) 3_to_8_decoder_74138_2: pin names not known; wires that end beside it: n4_to_1_mux_x2_74153_1_p13, n4_to_1_mux_x2_74153_4_p13, n4_to_1_mux_x2_74153_4_p14, 1'b1, n3_to_8_decoder_74138_1_p7, 1'b0, n3_to_8_decoder_74138_2_p7, n3_to_8_decoder_74138_2_p8, n3_to_8_decoder_74138_2_p9, n3_to_8_decoder_74138_2_p10, n3_to_8_decoder_74138_2_p11, n3_to_8_decoder_74138_2_p12, n3_to_8_decoder_74138_2_p13
  // _3_to_8_decoder__74138 #(.Facing("east")) 3_to_8_decoder_74138_3: pin names not known; wires that end beside it: n4_to_1_mux_x2_74153_2_p13, n4_to_1_mux_x2_74153_5_p13, n4_to_1_mux_x2_74153_5_p14, 1'b1, n3_to_8_decoder_74138_1_p8, 1'b0, n3_to_8_decoder_74138_3_p7, n3_to_8_decoder_74138_3_p8, n3_to_8_decoder_74138_3_p9, n3_to_8_decoder_74138_3_p10, n3_to_8_decoder_74138_3_p11, n3_to_8_decoder_74138_3_p12, n3_to_8_decoder_74138_3_p13
  // _3_to_8_decoder__74138 #(.Facing("east")) 3_to_8_decoder_74138_4: pin names not known; wires that end beside it: n4_to_1_mux_x2_74153_3_p14, n4_to_1_mux_x2_74153_3_p15, n4_to_1_mux_x2_74153_6_p9, 1'b1, n3_to_8_decoder_74138_1_p9, 1'b0, n3_to_8_decoder_74138_4_p7, n3_to_8_decoder_74138_4_p8, n3_to_8_decoder_74138_4_p9, n3_to_8_decoder_74138_4_p10, n3_to_8_decoder_74138_4_p11, n3_to_8_decoder_74138_4_p12, n3_to_8_decoder_74138_4_p13
  // _3_to_8_decoder__74138 #(.Facing("east")) 3_to_8_decoder_74138_5: pin names not known; wires that end beside it: n4_to_1_mux_x2_74153_7_p9, 1'b0, 1'b0, n3_to_8_decoder_74138_5_p4, n3_to_8_decoder_74138_5_p5
  // _3_to_8_decoder__74138 #(.Facing("east")) 3_to_8_decoder_74138_6: pin names not known; wires that end beside it: xor_1_out, xor_2_out, 1'b0, 1'b1, n3_to_8_decoder_74138_1_p10, 1'b0, n3_to_8_decoder_74138_6_p7, n3_to_8_decoder_74138_6_p8, n3_to_8_decoder_74138_6_p9, n3_to_8_decoder_74138_6_p10
  // _3_to_8_decoder__74138 #(.Facing("east")) 3_to_8_decoder_74138_7: pin names not known; wires that end beside it: and_3_out, and_4_out, 1'b0, 1'b1, n3_to_8_decoder_74138_1_p11, 1'b0, n3_to_8_decoder_74138_7_p7, n3_to_8_decoder_74138_7_p8, n3_to_8_decoder_74138_7_p9, n3_to_8_decoder_74138_7_p10
  // _3_to_8_decoder__74138 #(.Facing("east")) 3_to_8_decoder_74138_8: pin names not known; wires that end beside it: nor_2_out, nor_3_out, 1'b0, 1'b1, 1'b1, n3_to_8_decoder_74138_1_p12, n3_to_8_decoder_74138_1_p13, 1'b0, 1'b0, n3_to_8_decoder_74138_8_p10, n3_to_8_decoder_74138_8_p11, n3_to_8_decoder_74138_8_p12, n3_to_8_decoder_74138_8_p13
  and and_5 (and_5_out, n3_to_8_decoder_74138_2_p7, n3_to_8_decoder_74138_3_p7);
  and and_6 (and_6_out, n3_to_8_decoder_74138_2_p8, n3_to_8_decoder_74138_3_p8);
  and and_7 (and_7_out, n3_to_8_decoder_74138_2_p9, n3_to_8_decoder_74138_3_p9);
  and and_8 (and_8_out, n3_to_8_decoder_74138_2_p10, n3_to_8_decoder_74138_3_p10);
  and and_9 (and_9_out, and_5_out, n3_to_8_decoder_74138_4_p7);
  and and_10 (and_10_out, and_6_out, n3_to_8_decoder_74138_4_p8);
  and and_11 (and_11_out, and_7_out, n3_to_8_decoder_74138_4_p9);
  and and_12 (and_12_out, and_8_out, n3_to_8_decoder_74138_4_p10);
  and and_13 (and_13_out, and_9_out, n3_to_8_decoder_74138_6_p7);
  and and_14 (and_14_out, and_10_out, n3_to_8_decoder_74138_6_p8);
  and and_15 (and_15_out, and_11_out, n3_to_8_decoder_74138_6_p9);
  and and_16 (and_16_out, and_12_out, n3_to_8_decoder_74138_6_p10);
  and and_17 (and_17_out, and_13_out, n3_to_8_decoder_74138_7_p7);
  and and_18 (and_18_out, and_14_out, n3_to_8_decoder_74138_7_p8);
  and and_19 (and_19_out, and_15_out, n3_to_8_decoder_74138_7_p9);
  and and_20 (and_20_out, and_16_out, n3_to_8_decoder_74138_7_p10);
  and and_21 (and_21_out, and_17_out, n3_to_8_decoder_74138_8_p10);
  nand nand_1 (L0, and_21_out, n3_to_8_decoder_74138_5_p4);
  and and_22 (and_22_out, and_18_out, n3_to_8_decoder_74138_8_p11);
  and and_23 (and_23_out, and_22_out, n3_to_8_decoder_74138_3_p13);
  and and_24 (and_24_out, n3_to_8_decoder_74138_3_p12, n3_to_8_decoder_74138_3_p11);
  and and_25 (and_25_out, and_19_out, n3_to_8_decoder_74138_8_p12);
  and and_26 (and_26_out, and_20_out, n3_to_8_decoder_74138_8_p13);
  nand nand_2 (L4, n3_to_8_decoder_74138_2_p11, n3_to_8_decoder_74138_4_p11);
  nand nand_3 (L5, n3_to_8_decoder_74138_2_p12, n3_to_8_decoder_74138_4_p12);
  and and_27 (and_27_out, n3_to_8_decoder_74138_2_p13, n3_to_8_decoder_74138_4_p13);
  nand nand_4 (L1, and_23_out, n3_to_8_decoder_74138_5_p5);
  nand nand_5 (S, and_24_out, n3_to_8_decoder_74138_3_p13);
  nand nand_6 (L2, and_25_out, n3_to_8_decoder_74138_3_p12);
  nand nand_7 (L3, and_26_out, n3_to_8_decoder_74138_3_p11);
  not not_14 (L6, and_27_out);

  assign L0_2 = L0;
endmodule
